# Fritzing sketch motor (saved by Fritzing 0.9.3b)
breadboards: 1

parts:
  Part1 = Photon
  IC1 = L293D [package=THT]
  M1 = DC Motor
  VCC1 = 4 x AAA Battery Mount

nets:
  N1: Part1.A0, IC1.In_1
  N2: Part1.A1, IC1.In_2
  N3: Part1.GND, IC1.0V, VCC1.-
  N4: Part1.VIN, IC1.+Vmotor, IC1.+V, VCC1.+
  N5: Part1.D0, IC1.Enable_1
  N6: IC1.Out_1_(_Controlled_by_Enable_1_), M1.pin_2
  N7: IC1.Out_2_(_Controlled_by_Enable_1_), M1.pin_1
